// Logisim project TareaJueves.circ as structural Verilog: 1 circuit, main circuit main
module main (
  input  A,
  input  B,
  input  C,
  input  D
);

  wire and_1_out, and_2_out, and_3_out, and_4_out, and_5_out, and_6_out, and_7_out, and_8_out, not_1_out,
       not_2_out, not_3_out, not_4_out, not_5_out, not_6_out, not_7_out, not_8_out, not_9_out, not_10_out,
       not_11_out, not_12_out, or_1_out, or_2_out, or_3_out, or_4_out, or_5_out, or_6_out, or_7_out,
       or_8_out, or_9_out, or_10_out;

  not not_1 (not_1_out, C);
  not not_2 (not_2_out, D);
  not not_3 (not_3_out, B);
  not not_4 (not_4_out, D);
  not not_5 (not_5_out, B);
  and and_1 (and_1_out, not_1_out, not_2_out);
  and and_2 (and_2_out, C, D);
  or or_1 (or_1_out, B, not_6_out);
  not not_6 (not_6_out, C);
  not not_7 (not_7_out, A);
  not not_8 (not_8_out, B);
  not not_9 (not_9_out, B);
  not not_10 (not_10_out, D);
  not not_11 (not_11_out, D);
  not not_12 (not_12_out, C);
  and and_3 (and_3_out, B, D);
  and and_4 (and_4_out, not_3_out, not_4_out);
  and and_5 (and_5_out, not_7_out, not_8_out, C);
  and and_6 (and_6_out, not_9_out, not_10_out);
  and and_7 (and_7_out, C, not_11_out);
  and and_8 (and_8_out, B, not_12_out, D);
  or or_2 (or_2_out, and_3_out, and_4_out);
  or or_3 (or_3_out, not_5_out, and_1_out);
  or or_4 (or_4_out, or_1_out, D);
  or or_5 (or_5_out, and_5_out, and_6_out);
  or or_6 (or_6_out, and_7_out, and_8_out);
  or or_7 (or_7_out, A, or_2_out);
  or or_8 (or_8_out, or_3_out, and_2_out);
  or or_9 (or_9_out, or_5_out, or_6_out);
  or or_10 (or_10_out, C, or_7_out);
  _7_Segment_Display u_7_segment_display_1 (
    .a(or_10_out), .b(or_8_out), .d(or_9_out), .c(or_4_out));  // open: g, f, e, dp
endmodule
